// Logisim project 658_Computer.circ as structural Verilog: 3 circuits, main circuit Microcontroller
module Motherboard (
);

  wire TIMING_rst, TIMING_rst_1;
  wire [9:0] TIMING_selector;

  Timing_Circuit TIMING (.SELECTOR(TIMING_selector), .RST(TIMING_rst), .RST_1(TIMING_rst_1));  // open: CLK, CLK_B
  Microcontroller microcontroller_1 (.SELECTOR(TIMING_selector), .RST(TIMING_rst), .RST_1(TIMING_rst_1));
endmodule

module Microcontroller (
  input  [9:0] SELECTOR,
  input  RST,
  input  RST_1
);

  wire A_128K, and_3_out, and_4_out, and_5_out, and_6_out, and_7_out, and_9_out, and_10_out, BANK_LATCH,
       BANK_MAP, DEVICE_B, IDEVICE_0, IDMEM_INTERRUPT_COUNT, IDMEM_KERNAL_MODE, IDMEM_OUT_INTERRUPTS,
       IDMEM_USER_BANK, IREAD_ENABLE, IREAD_SELECT, IRQ_B, IRW_SELECT_B, IWRITE_ENABLE, IWRITE_SELECT,
       KERNAL_MODE, microprocessor_w65c816_1_p7, microprocessor_w65c816_1_p11, n4_bit_counter_lvc163_1_p4,
       nand_3_out, nand_5_out, nand_6_out, nand_7_out, nand_8_out, NMI_B, nor_2_out, nor_3_out, not_1_out,
       not_3_out, not_4_out, not_5_out, not_6_out, not_7_out, not_8_out, not_9_out, not_10_out, not_11_out,
       not_12_out, not_13_out, not_14_out, not_15_out, not_16_out, not_17_out, not_18_out, or_1_out,
       or_2_out, or_3_out, or_4_out, PHI2, pull_resistor_2_node, pull_resistor_3_node, pull_resistor_4_node,
       pull_resistor_7_node, pull_resistor_8_node, pull_resistor_9_node, pull_resistor_10_node,
       pull_resistor_11_node, pull_resistor_12_node, RESET, RWB, VALID_ADDRESS_B, VDA, VP_B, VPA;
  wire [2:0] n8_bit_latch_lvc573_1_p2;
  wire [3:0] n4_bit_counter_lvc163_1_p3, n4_bit_counter_lvc163_2_p3;
  wire [7:0] A0_7, A8_15, BA0_7, D, IRAM_A0_7, pull_resistor_6_node, USER_BANK;
  wire [7:1] n3_to_8_decoder_lvc138_2_p5;
  wire [7:4] n3_to_8_decoder_lvc138_1_p5;
  wire [9:0] timing_circuit_1_selector;
  wire [16:0] IRAM_A;

  Timing_Circuit timing_circuit_1 (
    .SELECTOR({timing_circuit_1_selector[9:3], BANK_MAP, timing_circuit_1_selector[1:0]}), .RST(RESET));  // open: RST_1, CLK, CLK_B
  not not_1 (not_1_out, VP_B);
  Pull_Resistor #(.pull(1)) pull_resistor_1 (.node(NMI_B));
  and and_1 (PHI2, timing_circuit_1_selector[0], timing_circuit_1_selector[1]);
  not not_2 (BANK_LATCH, timing_circuit_1_selector[1]);
  nand nand_1 (IREAD_SELECT, timing_circuit_1_selector[7], timing_circuit_1_selector[9], timing_circuit_1_selector[8]);
  nand nand_2 (IWRITE_SELECT, timing_circuit_1_selector[8], timing_circuit_1_selector[9]);
  and and_2 (IRW_SELECT_B, timing_circuit_1_selector[8], timing_circuit_1_selector[7], timing_circuit_1_selector[9]);
  nor nor_1 (VALID_ADDRESS_B, VDA, VPA);
  not not_3 (not_3_out, BA0_7[0]);
  not not_4 (not_4_out, BA0_7[1]);
  not not_5 (not_5_out, BA0_7[2]);
  not not_6 (not_6_out, BA0_7[3]);
  not not_7 (not_7_out, BA0_7[4]);
  not not_8 (not_8_out, BA0_7[5]);
  not not_9 (not_9_out, BA0_7[6]);
  not not_10 (not_10_out, BA0_7[7]);
  and and_3 (and_3_out, A0_7[1], A0_7[2], A0_7[3], not_1_out);
  and and_4 (and_4_out, not_4_out, not_5_out, not_6_out);
  and and_5 (and_5_out, not_3_out, not_4_out, not_5_out, not_6_out);
  and and_6 (and_6_out, not_7_out, not_8_out, not_9_out, not_10_out);
  // Probe on A0_7
  not not_11 (not_11_out, nand_3_out);
  // Probe on {4'b0000, n8_bit_latch_lvc573_1_p2, A0_7[0]}
  nand nand_3 (nand_3_out, and_3_out, ~IRQ_B);  // NAND_Gate
  Pull_Resistor pull_resistor_2 (.node(pull_resistor_2_node));
  Pull_Resistor pull_resistor_3 (.node(pull_resistor_3_node));
  Pull_Resistor #(.pull(1)) pull_resistor_4 (.node(pull_resistor_4_node));
  and and_7 (and_7_out, A8_15[4], A8_15[5], A8_15[6], A8_15[7]);
  // _8_bit_Line_Driver__LVC541 8_bit_line_driver_lvc541_1: pin names not known; wires that end beside it: not_11_out, not_11_out, A0_7, IRAM_A0_7
  // _8_bit_Latch__LVC573 8_bit_latch_lvc573_1: pin names not known; wires that end beside it: nand_3_out, {4'b0000, n8_bit_latch_lvc573_1_p2, A0_7[0]}, pull_resistor_2_node, IRAM_A0_7
  // _8_to_3_Encoder__LS148 8_to_3_encoder_ls148_1: pin names not known; wires that end beside it: pull_resistor_3_node, {8{1'b1}}, n8_bit_latch_lvc573_1_p2, IRQ_B
  // Microprocessor__W65C816 microprocessor_w65c816_1: pin names not known; wires that end beside it: pull_resistor_4_node, IRQ_B, NMI_B, RESET, PHI2, {A8_15, A0_7}, microprocessor_w65c816_1_p7, RWB, VDA, VPA, microprocessor_w65c816_1_p11, VP_B
  nand nand_4 (DEVICE_B, ~A8_15[3], and_7_out, and_5_out, and_6_out);  // NAND_Gate
  and and_8 (A_128K, and_4_out, and_6_out);
  // Probe on IRAM_A0_7
  Pull_Resistor #(.pull(1)) pull_resistor_5 (.node(microprocessor_w65c816_1_p11));
  // Probe on {A8_15, A0_7}
  // Probe on microprocessor_w65c816_1_p7
  Pull_Resistor pull_resistor_6 (.node(pull_resistor_6_node));
  not not_12 (not_12_out, KERNAL_MODE);
  and and_9 (and_9_out, A0_7[7], A8_15[0], A8_15[1], A8_15[2]);
  Pull_Resistor #(.pull(1)) pull_resistor_7 (.node(pull_resistor_7_node));
  Pull_Resistor pull_resistor_8 (.node(pull_resistor_8_node));
  not not_13 (not_13_out, PHI2);
  Pull_Resistor pull_resistor_9 (.node(pull_resistor_9_node));
  // _3_to_8_Decoder__LVC138 3_to_8_decoder_lvc138_1: pin names not known; wires that end beside it: IDEVICE_0, A0_7[3], A0_7[2:0], pull_resistor_7_node, {n3_to_8_decoder_lvc138_1_p5, IDMEM_OUT_INTERRUPTS, IDMEM_INTERRUPT_COUNT, IDMEM_USER_BANK, IDMEM_KERNAL_MODE}
  not not_14 (not_14_out, VP_B);
  not not_15 (not_15_out, RESET);
  Pull_Resistor #(.pull(1)) pull_resistor_10 (.node(pull_resistor_10_node));
  // _8_bit_Latch__LVC573 8_bit_latch_lvc573_2: pin names not known; wires that end beside it: pull_resistor_8_node, microprocessor_w65c816_1_p7, BANK_LATCH, BA0_7
  // _16_bit_Bus_Transceiver__LVC164245 16_bit_bus_transceiver_lvc164245_1: pin names not known; wires that end beside it: IRW_SELECT_B, not_13_out, PHI2, microprocessor_w65c816_1_p7, RWB, pull_resistor_6_node, pull_resistor_9_node, D, D, IREAD_SELECT, IWRITE_SELECT
  // _3_to_8_Decoder__LVC138 3_to_8_decoder_lvc138_2: pin names not known; wires that end beside it: not_12_out, DEVICE_B, A0_7[6:4], and_9_out, {n3_to_8_decoder_lvc138_2_p5, IDEVICE_0}
  nor nor_2 (nor_2_out, IDMEM_USER_BANK, RWB);
  nor nor_3 (nor_3_out, IDMEM_KERNAL_MODE, RWB);
  // Probe on BA0_7
  // Probe on D
  nand nand_5 (nand_5_out, ~IDMEM_USER_BANK, RWB);  // NAND_Gate
  Pull_Resistor pull_resistor_11 (.node(pull_resistor_11_node));
  nand nand_6 (nand_6_out, ~IDMEM_KERNAL_MODE, RWB);  // NAND_Gate
  or or_1 (or_1_out, D[0], not_14_out, not_15_out);
  // _4_bit_Counter__LVC163 4_bit_counter_lvc163_1: pin names not known; wires that end beside it: pull_resistor_10_node, RESET, n4_bit_counter_lvc163_1_p3, n4_bit_counter_lvc163_1_p4
  or or_2 (or_2_out, nor_3_out, not_14_out, not_15_out);
  and and_10 (and_10_out, or_2_out, PHI2);
  // _8_bit_Latch__LVC573 8_bit_latch_lvc573_3: pin names not known; wires that end beside it: pull_resistor_11_node, D, nor_2_out, USER_BANK
  D_Flip_Flop #(.trigger("high")) d_ff_1 (.clk(and_10_out), .D(or_1_out), .Q(KERNAL_MODE));  // open: Qn, preset, reset
  // Probe on KERNAL_MODE
  or or_3 (or_3_out, VDA, VPA);
  not not_16 (not_16_out, RWB);
  or or_4 (or_4_out, VDA, VPA);
  // Probe on USER_BANK
  // _4_bit_Counter__LVC163 4_bit_counter_lvc163_2: pin names not known; wires that end beside it: n4_bit_counter_lvc163_1_p4, RESET, n4_bit_counter_lvc163_2_p3
  and and_11 (IREAD_ENABLE, PHI2, RWB, or_3_out);
  and and_12 (IWRITE_ENABLE, PHI2, not_16_out, or_4_out);
  // _16_bit_Line_Driver__LVC16244 16_bit_line_driver_lvc16244_1: pin names not known; wires that end beside it: nand_5_out, nand_5_out, nand_6_out, nand_6_out, USER_BANK[7:4], USER_BANK[3:0], 4'b0000, {3'b000, KERNAL_MODE}, D[7:4], D[3:0], D[7:4], D[3:0]
  // _8_bit_Line_Driver__LVC541 8_bit_line_driver_lvc541_2: pin names not known; wires that end beside it: {n4_bit_counter_lvc163_2_p3, n4_bit_counter_lvc163_1_p3}
  not not_17 (not_17_out, KERNAL_MODE);
  not not_18 (not_18_out, KERNAL_MODE);
  nand nand_7 (nand_7_out, DEVICE_B, A_128K, IREAD_ENABLE);
  nand nand_8 (nand_8_out, DEVICE_B, A_128K, IWRITE_ENABLE);
  // Probe on IRAM_A
  RAM #(.addrWidth(17), .databus("bidir"), .enables("line"), .trigger("high"), .\type ("nonvolatile")) ram_1 (
    .addr(IRAM_A), .data(D));  // open: we, oe, clk
  // NOT_Gate not_19 has open pins: in=nand_7_out, out=open
  // NOT_Gate not_20 has open pins: in=nand_8_out, out=open
  Pull_Resistor pull_resistor_12 (.node(pull_resistor_12_node));
  // NOT_Gate not_21 has open pins: in=pull_resistor_12_node, out=open
  // _4_bit_Line_Driver__LVC126 4_bit_line_driver_lvc126_1: pin names not known; wires that end beside it: not_17_out, KERNAL_MODE, 1'b1, BA0_7[0], IRAM_A[16], IRAM_A[16]
  // _16_bit_Line_Driver__LVC16244 16_bit_line_driver_lvc16244_2: pin names not known; wires that end beside it: KERNAL_MODE, KERNAL_MODE, KERNAL_MODE, KERNAL_MODE, BA0_7[3:0], BA0_7[7:4], USER_BANK[3:0], USER_BANK[7:4], IRAM_A[3:0], IRAM_A[7:4], IRAM_A[11:8], IRAM_A[15:12]
  // _16_bit_Line_Driver__LVC16244 16_bit_line_driver_lvc16244_3: pin names not known; wires that end beside it: not_18_out, not_18_out, not_18_out, not_18_out, IRAM_A0_7[3:0], IRAM_A0_7[7:4], A8_15[3:0], A8_15[7:4], IRAM_A[3:0], IRAM_A[7:4], IRAM_A[11:8], IRAM_A[15:12]
  // Probe on D

  // Other names for the same wires on the sheet: DEVICE_A0_3[3:0] = A0_7[3:0];
  //   DEVICE_N0_6[6:0] = {A8_15[2:0], A0_7[7:4]}; IRAM_A8_15[7:0] = A8_15; IRAM_A16 = BA0_7[0]

  // Notes on the sheet:
  //   Device Decode (F000 to F7FF)
  //   Valid Address
  //   Bank Decode
  //   Internal Device Select
endmodule

module Timing_Circuit (
  output [9:0] SELECTOR,
  output RST,
  output RST_1,
  output CLK,
  output CLK_B
);

  wire and_1_out, and_2_out, clock_1_out, nand_1_out, nand_2_out, pull_resistor_1_node, pull_resistor_2_node,
       pull_resistor_3_node, pull_resistor_4_node, pull_resistor_5_node, pull_resistor_6_node,
       pull_resistor_7_node, pull_resistor_8_node;
  wire [3:0] n4_bit_counter_lvc163_1_p7, n4_bit_counter_lvc163_2_p7;
  wire [7:5] n3_to_8_decoder_lvc138_1_p5, n3_to_8_decoder_lvc138_2_p5;

  Clock clock_1 (.out(clock_1_out));
  // EconoReset__DS1813 econoreset_ds1813_1: pin names not known; wires that end beside it: clock_1_out, RST
  Clock clock_2 (.out(CLK));
  not not_1 (CLK_B, CLK);
  D_Flip_Flop d_ff_1 (.clk(CLK), .D(RST), .Q(RST_1));  // open: Qn, preset, reset
  and and_1 (and_1_out, RST, nand_1_out);
  and and_2 (and_2_out, RST, nand_2_out);
  Pull_Resistor #(.pull(1)) pull_resistor_1 (.node(pull_resistor_1_node));
  Pull_Resistor #(.pull(1)) pull_resistor_2 (.node(pull_resistor_2_node));
  Pull_Resistor #(.pull(1)) pull_resistor_3 (.node(pull_resistor_3_node));
  Pull_Resistor #(.pull(1)) pull_resistor_4 (.node(pull_resistor_4_node));
  Pull_Resistor #(.pull(1)) pull_resistor_5 (.node(pull_resistor_5_node));
  Pull_Resistor #(.pull(1)) pull_resistor_6 (.node(pull_resistor_6_node));
  // _4_bit_Counter__LVC163 4_bit_counter_lvc163_1: pin names not known; wires that end beside it: and_1_out, pull_resistor_1_node, pull_resistor_2_node, CLK_B, pull_resistor_3_node, RST_1, n4_bit_counter_lvc163_1_p7
  // _4_bit_Counter__LVC163 4_bit_counter_lvc163_2: pin names not known; wires that end beside it: and_2_out, pull_resistor_4_node, pull_resistor_5_node, CLK, pull_resistor_6_node, RST_1, n4_bit_counter_lvc163_2_p7
  nand nand_1 (nand_1_out, ~n4_bit_counter_lvc163_1_p7[0], ~n4_bit_counter_lvc163_1_p7[1], n4_bit_counter_lvc163_1_p7[2], ~n4_bit_counter_lvc163_1_p7[3]);  // NAND_Gate
  nand nand_2 (nand_2_out, ~n4_bit_counter_lvc163_2_p7[0], ~n4_bit_counter_lvc163_2_p7[1], n4_bit_counter_lvc163_2_p7[2], ~n4_bit_counter_lvc163_2_p7[3]);  // NAND_Gate
  Pull_Resistor pull_resistor_7 (.node(pull_resistor_7_node));
  Pull_Resistor pull_resistor_8 (.node(pull_resistor_8_node));
  // _3_to_8_Decoder__LVC138 3_to_8_decoder_lvc138_1: pin names not known; wires that end beside it: pull_resistor_7_node, pull_resistor_7_node, n4_bit_counter_lvc163_1_p7[2:0], RST, {n3_to_8_decoder_lvc138_1_p5, SELECTOR[8], SELECTOR[6], SELECTOR[4], SELECTOR[2], SELECTOR[0]}
  // _3_to_8_Decoder__LVC138 3_to_8_decoder_lvc138_2: pin names not known; wires that end beside it: pull_resistor_8_node, pull_resistor_8_node, n4_bit_counter_lvc163_2_p7[2:0], RST_1, {n3_to_8_decoder_lvc138_2_p5, SELECTOR[7], SELECTOR[5], SELECTOR[3], SELECTOR[1], SELECTOR[9]}
  Pull_Resistor #(.pull(1)) pull_resistor_9 (.node(n3_to_8_decoder_lvc138_1_p5[5]));
  Pull_Resistor #(.pull(1)) pull_resistor_10 (.node(n3_to_8_decoder_lvc138_1_p5[6]));
  Pull_Resistor #(.pull(1)) pull_resistor_11 (.node(n3_to_8_decoder_lvc138_1_p5[7]));
  Pull_Resistor #(.pull(1)) pull_resistor_12 (.node(n3_to_8_decoder_lvc138_2_p5[5]));
  Pull_Resistor #(.pull(1)) pull_resistor_13 (.node(n3_to_8_decoder_lvc138_2_p5[6]));
  Pull_Resistor #(.pull(1)) pull_resistor_14 (.node(n3_to_8_decoder_lvc138_2_p5[7]));
  // Digital_Oscilloscope #(.nState(16)) digital_oscilloscope_1: pin names not known; wires that end beside it: CLK, SELECTOR[0], SELECTOR[1], SELECTOR[2], SELECTOR[3], SELECTOR[4], SELECTOR[5], SELECTOR[6], SELECTOR[7], SELECTOR[8], SELECTOR[9]

  // Other names for the same wires on the sheet: CLOCK_B = CLK_B; RESET_0 = RST; RESET_1 = RST_1
endmodule
